# Fritzing sketch 230v-6v (saved by Fritzing 0.9.6b)
breadboards: 1

parts:
  5A_Fuse = FUSE [package=fuse_5mm]
  Z1 = VARISTOR [package=0603-res]
  R1 = Resistor [tolerance=±5% resistance=1000 package="0402 [SMD]"]
  C1 = Capacitor [package=0603-cap]
  D1 = bridge rectifier round [package="round [THT]"]
  C2 = Capacitor Polarized [package=panasonic_d]
  R2 = Resistor [tolerance=±5% resistance=1000 package="0402 [SMD]"]
  D2 = Zener Diode [part_number=1N4732A breakdown_voltage=3.6V package="300 mil [THT]"]
  R3 = Resistor [tolerance=±5% resistance=1000 package="0402 [SMD]"]
  LED1 = smd LED [color="Red (633nm)" package="0805 [SMD]"]
  R4 = Resistor [tolerance=±5% resistance=1000 package="0402 [SMD]"]
  Power_plug1 = Power plug

nets:
  N1: 5A_Fuse.1, Power_plug1.GND
  N2: 5A_Fuse.2, Z1.1, R1.Pin_0, C1.2
  N3: Z1.2, D1.DC-, R4.Pin_1
  N4: R1.Pin_1, C1.1, D1.DC+
  N5: D1.AC#0, C2.+, R2.Pin_0
  N6: D1.AC#1, C2.-, D2.anode, LED1.cathode
  N7: R2.Pin_1, D2.cathode, R3.Pin_1
  N8: R3.Pin_0, LED1.anode
  N9: R4.Pin_0, Power_plug1.VCC
